# Fritzing sketch Diagram (saved by Fritzing 0.9.3b)

parts:
  Part1 = Arduino Uno (Rev3)
  U2 = 74HC595 SMD [package="SO16 [SMD]"]
  Disp1 = LBT2088AH [part_number=LBT2088AH]
  Part2 = Thumb Joystick

nets:
  N1: Part1.A0, Part2.HORZ
  N2: Part1.A1, Part2.VERT
  N3: Part1.D8, Disp1.pin2
  N4: Part1.D9_PWM, Disp1.pin1
  N5: Part1.D11_PWM/MOSI, U2.DS
  N6: Part1.D13/SCK, U2.SH_CP, U2.ST_CP
  GND: Part1.GND, U2.OE, Part2.GND
  N7: Part1.D2, Disp1.pin_8
  N8: Part1.D3_PWM, Disp1.pin_7
  N9: Part1.D4, Disp1.pin_6
  N10: Part1.D5_PWM, Disp1.pin_5
  N11: Part1.D6_PWM, Disp1.pin_4
  N12: Part1.D7, Disp1.pin_3
  5V: Part1.5V, U2.VCC
  N13: U2.Q1, Disp1.pin_15
  N14: U2.Q2, Disp1.pin_14
  N15: U2.Q3, Disp1.pin_13
  N16: U2.Q4, Disp1.pin_12
  N17: U2.Q5, Disp1.pin_11
  N18: U2.Q6, Disp1.pin_10
  N19: U2.Q7, Disp1.pin_9
  N20: U2.Q0, Disp1.pin_16
